# Fritzing sketch fritzing_diagram (saved by Fritzing 0.9.9b)
breadboards: 1

parts:
  S1 = Pushbutton [package="[THT]"]
  R1 = Resistor [tolerance=±5% power=0.25 resistance=220 package=THT]
  S2 = Pushbutton [package="[THT]"]
  R2 = Resistor [tolerance=±5% power=0.25 resistance=220 package=THT]
  LED1 = RGB LED (com. cathode, rgb) [package="5 mm [THT]"]
  R3 = Resistor [tolerance=±5% power=0.25 resistance=220 package=THT]

nets:
  N1: S1.Pin_1, S1.Pin_2, S2.Pin_1, R3.Pin_1
  N2: S1.Pin_3, S1.Pin_4, R1.Pin_0
  N3: R1.Pin_1, R2.Pin_1
  N4: S2.Pin_3, S2.Pin_4, R2.Pin_0
  N5: LED1.common_cathode, R3.Pin_0
