# Fritzing sketch plan (saved by Fritzing 0.9.9b)
breadboards: 1

parts:
  S1 = Pushbutton [package="[THT]"]
  R1 = Resistor [tolerance=±5% power=0.25 resistance=220 package=THT]
  RHT1 = Humidity and Temperature Sensor RHT03
  R2 = Resistor [tolerance=±5% power=0.25 resistance=220 package=THT]

nets:
  N1: S1.Pin_1, S1.Pin_2, RHT1.GND_2
  N2: S1.Pin_3, S1.Pin_4, R1.Pin_1
  N3: R1.Pin_0, RHT1.Vcc, R2.Pin_0
  N4: RHT1.Data-signal, R2.Pin_1
